// Logisim project 16BitCPU.circ as structural Verilog: 1 circuit, main circuit main
module main (
);

  wire A_IN, A_OUT, ALU_OUT, B_IN, B_OUT, CARRY_FLAG, CLK, counter_2_carry, decoder_1_out0, decoder_1_out1,
       decoder_1_out2, decoder_1_out3, decoder_1_out4, decoder_1_out5, decoder_1_out6, decoder_1_out7,
       FLAGS_IN, INST_IN, not_1_out, or_1_out, PC_ENABLE, PC_IN, PC_OUT, pull_resistor_1_node,
       pull_resistor_2_node, pull_resistor_3_node, pull_resistor_4_node, RAM_ADDR, RAM_IN, RAM_OUT,
       RESET_MICRO_STEP, RST, ZERO_FLAG;
  wire [0:0] rom_7_data;
  wire [1:0] FLAGS;
  wire [2:0] ALU_OP;
  wire [3:0] ALU_NIBBLE_1, ALU_NIBBLE_2, ALU_NIBBLE_3, ALU_NIBBLE_4;
  wire [3:1] rom_5_data, rom_6_data, rom_7_data_2;
  wire [7:0] counter_2_q, counter_3_q, register_5_q_3, register_6_q;
  wire [7:1] rom_3_data;
  wire [7:5] rom_4_data;
  wire [9:0] counter_1_q;
  wire [11:0] register_5_q, register_5_q_2;
  wire [15:0] MAIN_BUS, ram_1_dout, register_1_q, register_2_q;

  not not_1 (not_1_out, CLK);
  Register #(.width(16)) register_1 (
    .D(MAIN_BUS), .en(RAM_ADDR), .Q(register_1_q), .clk(CLK), .clr(pull_resistor_1_node));
  Pull_Resistor pull_resistor_1 (.node(pull_resistor_1_node));
  Register #(.width(16)) register_2 (
    .D(MAIN_BUS), .en(RAM_IN), .Q(register_2_q), .clk(CLK), .clr(pull_resistor_2_node));
  Pull_Resistor pull_resistor_2 (.node(pull_resistor_2_node));
  Pull_Resistor pull_resistor_3 (.node(pull_resistor_3_node));
  Pull_Resistor #(.pull(1)) pull_resistor_4 (.node(pull_resistor_4_node));
  RAM #(.addrWidth(16), .dataWidth(16), .trigger("high")) ram_1 (
    .addr(register_1_q), .we(RAM_IN), .oe(RAM_OUT), .din(register_2_q), .dout(ram_1_dout));
  Register #(.width(6)) register_3 (.D(MAIN_BUS[15:10]), .en(INST_IN), .clk(CLK), .Q(counter_1_q[5:0]));  // open: clr
  Counter #(.max('hf), .width(4)) counter_1 (
    .load(pull_resistor_3_node), .count(pull_resistor_4_node), .Q(counter_1_q[9:6]), .up(1'b1),
    .clk(not_1_out), .clr(RESET_MICRO_STEP));  // open: D, carry
  ROM #(.addrWidth(12)) rom_1 (
    .addr({FLAGS, counter_1_q}), .data({PC_IN, RAM_ADDR, RAM_OUT, RAM_IN, B_OUT, B_IN, A_OUT, A_IN}));
  ROM #(.addrWidth(12)) rom_2 (
    .addr({FLAGS, counter_1_q}), .data({INST_IN, FLAGS_IN, ALU_OP, ALU_OUT, PC_ENABLE, PC_OUT}));
  ROM #(.addrWidth(12)) rom_3 (.addr({FLAGS, counter_1_q}), .data({rom_3_data, RESET_MICRO_STEP}));
  Hex_Digit_Display hex_digit_display_1 (.value(counter_1_q[9:6]));  // open: dp
  assign MAIN_BUS = RAM_OUT ? ram_1_dout : 16'bz;  // Controlled_Buffer controlled_buffer_1
  LED led_1 (.in(MAIN_BUS[15]));
  LED led_2 (.in(MAIN_BUS[14]));
  LED led_3 (.in(A_IN));
  LED led_4 (.in(A_OUT));
  LED led_5 (.in(B_IN));
  LED led_6 (.in(B_OUT));
  LED led_7 (.in(RAM_IN));
  LED led_8 (.in(RAM_OUT));
  LED led_9 (.in(RAM_ADDR));
  LED led_10 (.in(PC_IN));
  LED led_11 (.in(PC_OUT));
  LED led_12 (.in(PC_ENABLE));
  LED led_13 (.in(ALU_OUT));
  LED led_14 (.in(ALU_OP[0]));
  LED led_15 (.in(ALU_OP[1]));
  LED led_16 (.in(ALU_OP[2]));
  LED led_17 (.in(FLAGS_IN));
  LED led_18 (.in(INST_IN));
  LED led_19 (.in(RESET_MICRO_STEP));
  LED led_20 (.in(MAIN_BUS[13]));
  LED led_21 (.in(MAIN_BUS[12]));
  LED led_22 (.in(MAIN_BUS[11]));
  LED led_23 (.in(MAIN_BUS[10]));
  Clock clock_1 (.out(CLK));
  LED led_24 (.in(MAIN_BUS[9]));
  LED led_25 (.in(MAIN_BUS[8]));
  LED led_26 (.in(MAIN_BUS[7]));
  LED led_27 (.in(MAIN_BUS[6]));
  LED led_28 (.in(MAIN_BUS[5]));
  LED led_29 (.in(MAIN_BUS[4]));
  LED led_30 (.in(MAIN_BUS[3]));
  LED led_31 (.in(MAIN_BUS[2]));
  Pull_Resistor pull_resistor_5 (.node(MAIN_BUS));
  LED led_32 (.in(MAIN_BUS[1]));
  LED led_33 (.in(MAIN_BUS[0]));
  not not_2 (ZERO_FLAG, or_1_out);
  or or_1 (or_1_out, ALU_NIBBLE_1[0], ALU_NIBBLE_1[1], ALU_NIBBLE_1[2], ALU_NIBBLE_1[3], ALU_NIBBLE_2[0], ALU_NIBBLE_2[1], ALU_NIBBLE_2[2], ALU_NIBBLE_2[3], ALU_NIBBLE_3[0], ALU_NIBBLE_3[1], ALU_NIBBLE_3[2], ALU_NIBBLE_3[3], ALU_NIBBLE_4[0], ALU_NIBBLE_4[1], ALU_NIBBLE_4[2], ALU_NIBBLE_4[3]);
  ROM #(.addrWidth(13)) rom_4 (
    .addr({1'b0, register_5_q_2[11:8], ALU_OP, register_5_q_2[4:0]}),
    .data({rom_4_data, CARRY_FLAG, ALU_NIBBLE_4}));
  Decoder #(.enable("false"), .select(3)) decoder_1 (
    .out0(decoder_1_out0), .out1(decoder_1_out1), .out2(decoder_1_out2), .out3(decoder_1_out3),
    .out4(decoder_1_out4), .out5(decoder_1_out5), .out6(decoder_1_out6), .out7(decoder_1_out7), .sel(ALU_OP));
  Counter counter_2 (
    .load(PC_IN), .D(MAIN_BUS[7:0]), .count(PC_ENABLE), .Q(counter_2_q), .carry(counter_2_carry), .up(1'b1),
    .clk(CLK), .clr(RST));
  assign MAIN_BUS[7:0] = PC_OUT ? counter_2_q : 8'bz;  // Controlled_Buffer controlled_buffer_2
  assign MAIN_BUS[15:8] = PC_OUT ? counter_3_q : 8'bz;  // Controlled_Buffer controlled_buffer_3
  Register #(.width(2)) register_4 (.D({CARRY_FLAG, ZERO_FLAG}), .en(FLAGS_IN), .clk(CLK), .Q(FLAGS), .clr(RST));
  LED led_34 (.in(decoder_1_out0));
  LED led_35 (.in(decoder_1_out1));
  LED led_36 (.in(decoder_1_out2));
  LED led_37 (.in(decoder_1_out3));
  LED led_38 (.in(decoder_1_out4));
  LED led_39 (.in(decoder_1_out5));
  LED led_40 (.in(decoder_1_out6));
  LED led_41 (.in(decoder_1_out7));
  Counter counter_3 (
    .load(PC_IN), .D(MAIN_BUS[15:8]), .count(counter_2_carry), .Q(counter_3_q), .up(1'b1), .clk(CLK),
    .clr(RST));  // open: carry
  assign MAIN_BUS = ALU_OUT ? {ALU_NIBBLE_4, ALU_NIBBLE_3, ALU_NIBBLE_2, ALU_NIBBLE_1} : 16'bz;  // Controlled_Buffer controlled_buffer_4
  ROM #(.addrWidth(13)) rom_5 (
    .addr({1'b0, register_5_q[11:8], ALU_OP, register_5_q[4:0]}),
    .data({rom_5_data, register_5_q_2[0], ALU_NIBBLE_3}));
  Register #(.width(16)) register_5 (
    .D(MAIN_BUS), .en(A_IN), .clk(CLK), .Q({register_5_q_2[4:1], register_5_q[4:1], register_5_q_3}),
    .clr(RST));
  Register #(.width(16)) register_6 (
    .D(MAIN_BUS), .en(B_IN), .clk(CLK), .Q({register_5_q_2[11:8], register_5_q[11:8], register_6_q}),
    .clr(RST));
  assign MAIN_BUS = A_OUT ? {register_5_q_2[4:1], register_5_q[4:1], register_5_q_3} : 16'bz;  // Controlled_Buffer controlled_buffer_5
  assign MAIN_BUS = B_OUT ? {register_5_q_2[11:8], register_5_q[11:8], register_6_q} : 16'bz;  // Controlled_Buffer controlled_buffer_6
  ROM #(.addrWidth(13)) rom_6 (
    .addr({1'b0, register_6_q[7:4], ALU_OP, register_5_q_3[7:4], rom_7_data[0]}),
    .data({rom_6_data, register_5_q[0], ALU_NIBBLE_2}));
  Pull_Resistor pull_resistor_6 (.node(RST));
  ROM #(.addrWidth(13)) rom_7 (
    .addr({1'b0, register_6_q[3:0], ALU_OP, register_5_q_3[3:0], 1'b0}),
    .data({rom_7_data_2, rom_7_data[0], ALU_NIBBLE_1}));

  // Other names for the same wires on the sheet: ALU_OP1 = ALU_OP[0]; ALU_OP2 = ALU_OP[1]; ALU_OP3 = ALU_OP[2]

  // Notes on the sheet:
  //   contents of rom_1 (hex, n*v repeats v):
  //   64*40 64*20 0 1 4 1 4 0 1 1 1 11*40 0 0 40 40 49*0 60 24 60 24 60 21 60 24 60 60 a0 0 0 a0 a0 49*0
  //   24 1 24 1 21 0 24 0 12 18 54*0 1 0 1 692*0 64*40 64*20 0 1 4 1 4 0 1 1 1 11*40 0 40 40 50*0 60 24 60
  //   24 60 21 60 24 60 60 a0 0 a0 a0 50*0 24 1 24 1 21 0 24 0 12 18 54*0 1 0 1 692*0 64*40 64*20 0 1 4 1
  //   4 0 1 1 1 12*40 0 0 40 49*0 60 24 60 24 60 21 60 24 60 60 a0 a0 0 0 a0 49*0 24 1 24 1 21 0 24 0 12
  //   18 54*0 1 0 1 692*0 64*40 64*20 0 1 4 1 4 0 1 1 1 13*40 51*0 60 24 60 24 60 21 60 24 60 60 a0 a0 a0
  //   51*0 24 1 24 1 21 0 24 0 12 18 54*0 1 0 1
  //   contents of rom_2 (hex, n*v repeats v):
  //   64*1 64*82 0 44 44 4c 4c 0 64 54 5c 11*1 2 2 1 1 49*0 10*2 55*0 44 0 4c 60*0 44 0 4c 692*0 64*1
  //   64*82 0 44 44 4c 4c 0 64 54 5c 11*1 2 1 1 2 49*0 10*2 55*0 44 0 4c 60*0 44 0 4c 692*0 64*1 64*82 0
  //   44 44 4c 4c 0 64 54 5c 12*1 2 2 1 49*0 10*2 55*0 44 0 4c 60*0 44 0 4c 692*0 64*1 64*82 0 44 44 4c 4c
  //   0 64 54 5c 13*1 2 2 49*0 10*2 55*0 44 0 4c 60*0 44 0 4c
  //   contents of rom_3 (hex, n*v repeats v):
  //   128*0 1 4*0 1 18*0 49*1 11*0 1 1 0 0 49*1 5*0 1 0 1 0 0 54*1 0 1 0 692*1 128*0 1 4*0 1 18*0 49*1
  //   11*0 1 0 0 50*1 5*0 1 0 1 0 0 54*1 0 1 0 692*1 128*0 1 4*0 1 18*0 49*1 12*0 1 1 0 49*1 5*0 1 0 1 0 0
  //   54*1 0 1 0 692*1 128*0 1 4*0 1 18*0 49*1 13*0 51*1 5*0 1 0 1 0 0 54*1 0 1 0 692*1
  //   contents of rom_4 (hex, n*v repeats v):
  //   0 1 1 2 2 3 3 4 4 5 5 6 6 7 7 8 8 9 9 a a b b c c d d e e f f 10 f 10 10 11 11 12 12 13 13 14 14 15
  //   15 16 16 17 17 18 18 19 19 1a 1a 1b 1b 1c 1c 1d 1d 1e 1e 1f 34*0 1 1 2 2 3 3 4 4 5 5 6 6 7 7 8 8 9 9
  //   a a b b c c d d e e f f 0 0 1 1 2 2 3 3 4 4 5 5 6 6 7 7 8 8 9 9 a a b b c c d d e e f f 0 1 2 3 4 5
  //   6 7 8 9 a b c d e f 10 11 12 13 14 15 16 17 18 19 1a 1b 1c 1d 1e 1f 0 1 0 1 0 1 0 1 0 1 0 1 0 1 0 1
  //   0 1 0 1 0 1 0 1 0 1 0 1 0 1 0 1 0 0 1 1 2 2 3 3 4 4 5 5 6 6 7 7 8 8 9 9 a a b b c c d d e e f f 1 2
  //   2 3 3 4 4 5 5 6 6 7 7 8 8 9 9 a a b b c c d d e e f f 10 10 11 e f f 10 10 11 11 12 12 13 13 14 14
  //   15 15 16 16 17 17 18 18 19 19 1a 1a 1b 1b 1c 1c 1d 1d 1e 0 0 1 1 0 0 1 1 0 0 1 1 0 0 1 1 0 0 1 1 0 0
  //   1 1 0 0 1 1 0 0 6*1 4*3 4*5 4*7 4*9 4*b 4*d 4*f 1 1 0 0 3 3 2 2 5 5 4 4 7 7 6 6 9 9 8 8 b b a a d d
  //   c c f f e e 0 1 2 3 4 5 6 7 8 9 a b c d e f 10 11 12 13 14 15 16 17 18 19 1a 1b 1c 1d 1e 1f 2 3 2 3
  //   2 3 2 3 2 3 2 3 2 3 2 3 2 3 2 3 2 3 2 3 2 3 2 3 2 3 2 3 0 0 1 1 2 2 3 3 4 4 5 5 6 6 7 7 8 8 9 9 a a
  //   b b c c d d e e f f 2 3 3 4 4 5 5 6 6 7 7 8 8 9 9 a a b b c c d d e e f f 10 10 11 11 12 d e e f f
  //   10 10 11 11 12 12 13 13 14 14 15 15 16 16 17 17 18 18 19 19 1a 1a 1b 1b 1c 1c 1d 4*0 4*2 4*0 4*2 4*0
  //   4*2 4*0 6*2 3 3 2 2 3 3 6 6 7 7 6 6 7 7 a a b b a a b b e e f f e e f f 2 2 3 3 0 0 1 1 6 6 7 7 4 4
  //   5 5 a a b b 8 8 9 9 e e f f c c d d 0 1 2 3 4 5 6 7 8 9 a b c d e f 10 11 12 13 14 15 16 17 18 19 1a
  //   1b 1c 1d 1e 1f 4 5 4 5 4 5 4 5 4 5 4 5 4 5 4 5 4 5 4 5 4 5 4 5 4 5 4 5 4 5 4 5 0 0 1 1 2 2 3 3 4 4 5
  //   5 6 6 7 7 8 8 9 9 a a b b c c d d e e f f 3 4 4 5 5 6 6 7 7 8 8 9 9 a a b b c c d d e e f f 10 10 11
  //   11 12 12 13 c d d e e f f 10 10 11 11 12 12 13 13 14 14 15 15 16 16 17 17 18 18 19 19 1a 1a 1b 1b 1c
  //   0 0 1 1 2 2 3 3 0 0 1 1 2 2 3 3 0 0 1 1 2 2 3 3 0 0 1 1 2 2 10*3 8*7 8*b 8*f 3 3 2 2 1 1 0 0 7 7 6 6
  //   5 5 4 4 b b a a 9 9 8 8 f f e e d d c c 0 1 2 3 4 5 6 7 8 9 a b c d e f 10 11 12 13 14 15 16 17 18
  //   19 1a 1b 1c 1d 1e 1f 6 7 6 7 6 7 6 7 6 7 6 7 6 7 6 7 6 7 6 7 6 7 6 7 6 7 6 7 6 7 6 7 0 0 1 1 2 2 3 3
  //   4 4 5 5 6 6 7 7 8 8 9 9 a a b b c c d d e e f f 4 5 5 6 6 7 7 8 8 9 9 a a b b c c d d e e f f 10 10
  //   11 11 12 12 13 13 14 b c c d d e e f f 10 10 11 11 12 12 13 13 14 14 15 15 16 16 17 17 18 18 19 19
  //   1a 1a 1b 8*0 8*4 8*0 10*4 5 5 6 6 7 7 4 4 5 5 6 6 7 7 c c d d e e f f c c d d e e f f 4 4 5 5 6 6 7
  //   7 0 0 1 1 2 2 3 3 c c d d e e f f 8 8 9 9 a a b b 0 1 2 3 4 5 6 7 8 9 a b c d e f 10 11 12 13 14 15
  //   16 17 18 19 1a 1b 1c 1d 1e 1f 8 9 8 9 8 9 8 9 8 9 8 9 8 9 8 9 8 9 8 9 8 9 8 9 8 9 8 9 8 9 8 9 0 0 1
  //   1 2 2 3 3 4 4 5 5 6 6 7 7 8 8 9 9 a a b b c c d d e e f f 5 6 6 7 7 8 8 9 9 a a b b c c d d e e f f
  //   10 10 11 11 12 12 13 13 14 14 15 a b b c c d d e e f f 10 10 11 11 12 12 13 13 14 14 15 15 16 16 17
  //   17 18 18 19 19 1a 0 0 1 1 0 0 1 1 4 4 5 5 4 4 5 5 0 0 1 1 0 0 1 1 4 4 5 5 4 4 6*5 4*7 4*5 4*7 4*d
  //   4*f 4*d 4*f 5 5 4 4 7 7 6 6 1 1 0 0 3 3 2 2 d d c c f f e e 9 9 8 8 b b a a 0 1 2 3 4 5 6 7 8 9 a b
  //   c d e f 10 11 12 13 14 15 16 17 18 19 1a 1b 1c 1d 1e 1f a b a b a b a b a b a b a b a b a b a b a b
  //   a b a b a b a b a b 0 0 1 1 2 2 3 3 4 4 5 5 6 6 7 7 8 8 9 9 a a b b c c d d e e f f 6 7 7 8 8 9 9 a
  //   a b b c c d d e e f f 10 10 11 11 12 12 13 13 14 14 15 15 16 9 a a b b c c d d e e f f 10 10 11 11
  //   12 12 13 13 14 14 15 15 16 16 17 17 18 18 19 4*0 4*2 4*4 4*6 4*0 4*2 4*4 6*6 7 7 6 6 7 7 6 6 7 7 6 6
  //   7 7 e e f f e e f f e e f f e e f f 6 6 7 7 4 4 5 5 2 2 3 3 0 0 1 1 e e f f c c d d a a b b 8 8 9 9
  //   0 1 2 3 4 5 6 7 8 9 a b c d e f 10 11 12 13 14 15 16 17 18 19 1a 1b 1c 1d 1e 1f c d c d c d c d c d
  //   c d c d c d c d c d c d c d c d c d c d c d 0 0 1 1 2 2 3 3 4 4 5 5 6 6 7 7 8 8 9 9 a a b b c c d d
  //   e e f f 7 8 8 9 9 a a b b c c d d e e f f 10 10 11 11 12 12 13 13 14 14 15 15 16 16 17 8 9 9 a a b b
  //   c c d d e e f f 10 10 11 11 12 12 13 13 14 14 15 15 16 16 17 17 18 0 0 1 1 2 2 3 3 4 4 5 5 6 6 7 7 0
  //   0 1 1 2 2 3 3 4 4 5 5 6 6 18*7 16*f 7 7 6 6 5 5 4 4 3 3 2 2 1 1 0 0 f f e e d d c c b b a a 9 9 8 8
  //   0 1 2 3 4 5 6 7 8 9 a b c d e f 10 11 12 13 14 15 16 17 18 19 1a 1b 1c 1d 1e 1f e f e f e f e f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
  //   Program Counter - 16Bit
  //   ADD
  //   SUB
  //   AND
  //   OR
  //   XOR
  //   SHLA
  //   SHLB
  //   DIV
  //   contents of rom_5 (hex, n*v repeats v):
  //   0 1 1 2 2 3 3 4 4 5 5 6 6 7 7 8 8 9 9 a a b b c c d d e e f f 10 f 10 10 11 11 12 12 13 13 14 14 15
  //   15 16 16 17 17 18 18 19 19 1a 1a 1b 1b 1c 1c 1d 1d 1e 1e 1f 34*0 1 1 2 2 3 3 4 4 5 5 6 6 7 7 8 8 9 9
  //   a a b b c c d d e e f f 0 0 1 1 2 2 3 3 4 4 5 5 6 6 7 7 8 8 9 9 a a b b c c d d e e f f 0 1 2 3 4 5
  //   6 7 8 9 a b c d e f 10 11 12 13 14 15 16 17 18 19 1a 1b 1c 1d 1e 1f 0 1 0 1 0 1 0 1 0 1 0 1 0 1 0 1
  //   0 1 0 1 0 1 0 1 0 1 0 1 0 1 0 1 0 0 1 1 2 2 3 3 4 4 5 5 6 6 7 7 8 8 9 9 a a b b c c d d e e f f 1 2
  //   2 3 3 4 4 5 5 6 6 7 7 8 8 9 9 a a b b c c d d e e f f 10 10 11 e f f 10 10 11 11 12 12 13 13 14 14
  //   15 15 16 16 17 17 18 18 19 19 1a 1a 1b 1b 1c 1c 1d 1d 1e 0 0 1 1 0 0 1 1 0 0 1 1 0 0 1 1 0 0 1 1 0 0
  //   1 1 0 0 1 1 0 0 6*1 4*3 4*5 4*7 4*9 4*b 4*d 4*f 1 1 0 0 3 3 2 2 5 5 4 4 7 7 6 6 9 9 8 8 b b a a d d
  //   c c f f e e 0 1 2 3 4 5 6 7 8 9 a b c d e f 10 11 12 13 14 15 16 17 18 19 1a 1b 1c 1d 1e 1f 2 3 2 3
  //   2 3 2 3 2 3 2 3 2 3 2 3 2 3 2 3 2 3 2 3 2 3 2 3 2 3 2 3 0 0 1 1 2 2 3 3 4 4 5 5 6 6 7 7 8 8 9 9 a a
  //   b b c c d d e e f f 2 3 3 4 4 5 5 6 6 7 7 8 8 9 9 a a b b c c d d e e f f 10 10 11 11 12 d e e f f
  //   10 10 11 11 12 12 13 13 14 14 15 15 16 16 17 17 18 18 19 19 1a 1a 1b 1b 1c 1c 1d 4*0 4*2 4*0 4*2 4*0
  //   4*2 4*0 6*2 3 3 2 2 3 3 6 6 7 7 6 6 7 7 a a b b a a b b e e f f e e f f 2 2 3 3 0 0 1 1 6 6 7 7 4 4
  //   5 5 a a b b 8 8 9 9 e e f f c c d d 0 1 2 3 4 5 6 7 8 9 a b c d e f 10 11 12 13 14 15 16 17 18 19 1a
  //   1b 1c 1d 1e 1f 4 5 4 5 4 5 4 5 4 5 4 5 4 5 4 5 4 5 4 5 4 5 4 5 4 5 4 5 4 5 4 5 0 0 1 1 2 2 3 3 4 4 5
  //   5 6 6 7 7 8 8 9 9 a a b b c c d d e e f f 3 4 4 5 5 6 6 7 7 8 8 9 9 a a b b c c d d e e f f 10 10 11
  //   11 12 12 13 c d d e e f f 10 10 11 11 12 12 13 13 14 14 15 15 16 16 17 17 18 18 19 19 1a 1a 1b 1b 1c
  //   0 0 1 1 2 2 3 3 0 0 1 1 2 2 3 3 0 0 1 1 2 2 3 3 0 0 1 1 2 2 10*3 8*7 8*b 8*f 3 3 2 2 1 1 0 0 7 7 6 6
  //   5 5 4 4 b b a a 9 9 8 8 f f e e d d c c 0 1 2 3 4 5 6 7 8 9 a b c d e f 10 11 12 13 14 15 16 17 18
  //   19 1a 1b 1c 1d 1e 1f 6 7 6 7 6 7 6 7 6 7 6 7 6 7 6 7 6 7 6 7 6 7 6 7 6 7 6 7 6 7 6 7 0 0 1 1 2 2 3 3
  //   4 4 5 5 6 6 7 7 8 8 9 9 a a b b c c d d e e f f 4 5 5 6 6 7 7 8 8 9 9 a a b b c c d d e e f f 10 10
  //   11 11 12 12 13 13 14 b c c d d e e f f 10 10 11 11 12 12 13 13 14 14 15 15 16 16 17 17 18 18 19 19
  //   1a 1a 1b 8*0 8*4 8*0 10*4 5 5 6 6 7 7 4 4 5 5 6 6 7 7 c c d d e e f f c c d d e e f f 4 4 5 5 6 6 7
  //   7 0 0 1 1 2 2 3 3 c c d d e e f f 8 8 9 9 a a b b 0 1 2 3 4 5 6 7 8 9 a b c d e f 10 11 12 13 14 15
  //   16 17 18 19 1a 1b 1c 1d 1e 1f 8 9 8 9 8 9 8 9 8 9 8 9 8 9 8 9 8 9 8 9 8 9 8 9 8 9 8 9 8 9 8 9 0 0 1
  //   1 2 2 3 3 4 4 5 5 6 6 7 7 8 8 9 9 a a b b c c d d e e f f 5 6 6 7 7 8 8 9 9 a a b b c c d d e e f f
  //   10 10 11 11 12 12 13 13 14 14 15 a b b c c d d e e f f 10 10 11 11 12 12 13 13 14 14 15 15 16 16 17
  //   17 18 18 19 19 1a 0 0 1 1 0 0 1 1 4 4 5 5 4 4 5 5 0 0 1 1 0 0 1 1 4 4 5 5 4 4 6*5 4*7 4*5 4*7 4*d
  //   4*f 4*d 4*f 5 5 4 4 7 7 6 6 1 1 0 0 3 3 2 2 d d c c f f e e 9 9 8 8 b b a a 0 1 2 3 4 5 6 7 8 9 a b
  //   c d e f 10 11 12 13 14 15 16 17 18 19 1a 1b 1c 1d 1e 1f a b a b a b a b a b a b a b a b a b a b a b
  //   a b a b a b a b a b 0 0 1 1 2 2 3 3 4 4 5 5 6 6 7 7 8 8 9 9 a a b b c c d d e e f f 6 7 7 8 8 9 9 a
  //   a b b c c d d e e f f 10 10 11 11 12 12 13 13 14 14 15 15 16 9 a a b b c c d d e e f f 10 10 11 11
  //   12 12 13 13 14 14 15 15 16 16 17 17 18 18 19 4*0 4*2 4*4 4*6 4*0 4*2 4*4 6*6 7 7 6 6 7 7 6 6 7 7 6 6
  //   7 7 e e f f e e f f e e f f e e f f 6 6 7 7 4 4 5 5 2 2 3 3 0 0 1 1 e e f f c c d d a a b b 8 8 9 9
  //   0 1 2 3 4 5 6 7 8 9 a b c d e f 10 11 12 13 14 15 16 17 18 19 1a 1b 1c 1d 1e 1f c d c d c d c d c d
  //   c d c d c d c d c d c d c d c d c d c d c d 0 0 1 1 2 2 3 3 4 4 5 5 6 6 7 7 8 8 9 9 a a b b c c d d
  //   e e f f 7 8 8 9 9 a a b b c c d d e e f f 10 10 11 11 12 12 13 13 14 14 15 15 16 16 17 8 9 9 a a b b
  //   c c d d e e f f 10 10 11 11 12 12 13 13 14 14 15 15 16 16 17 17 18 0 0 1 1 2 2 3 3 4 4 5 5 6 6 7 7 0
  //   0 1 1 2 2 3 3 4 4 5 5 6 6 18*7 16*f 7 7 6 6 5 5 4 4 3 3 2 2 1 1 0 0 f f e e d d c c b b a a 9 9 8 8
  //   0 1 2 3 4 5 6 7 8 9 a b c d e f 10 11 12 13 14 15 16 17 18 19 1a 1b 1c 1d 1e 1f e f e f e f e f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
  //   Register A - 16Bit
  //   Register B - 16Bit
  //   contents of rom_6 (hex, n*v repeats v):
  //   0 1 1 2 2 3 3 4 4 5 5 6 6 7 7 8 8 9 9 a a b b c c d d e e f f 10 f 10 10 11 11 12 12 13 13 14 14 15
  //   15 16 16 17 17 18 18 19 19 1a 1a 1b 1b 1c 1c 1d 1d 1e 1e 1f 34*0 1 1 2 2 3 3 4 4 5 5 6 6 7 7 8 8 9 9
  //   a a b b c c d d e e f f 0 0 1 1 2 2 3 3 4 4 5 5 6 6 7 7 8 8 9 9 a a b b c c d d e e f f 0 1 2 3 4 5
  //   6 7 8 9 a b c d e f 10 11 12 13 14 15 16 17 18 19 1a 1b 1c 1d 1e 1f 0 1 0 1 0 1 0 1 0 1 0 1 0 1 0 1
  //   0 1 0 1 0 1 0 1 0 1 0 1 0 1 0 1 0 0 1 1 2 2 3 3 4 4 5 5 6 6 7 7 8 8 9 9 a a b b c c d d e e f f 1 2
  //   2 3 3 4 4 5 5 6 6 7 7 8 8 9 9 a a b b c c d d e e f f 10 10 11 e f f 10 10 11 11 12 12 13 13 14 14
  //   15 15 16 16 17 17 18 18 19 19 1a 1a 1b 1b 1c 1c 1d 1d 1e 0 0 1 1 0 0 1 1 0 0 1 1 0 0 1 1 0 0 1 1 0 0
  //   1 1 0 0 1 1 0 0 6*1 4*3 4*5 4*7 4*9 4*b 4*d 4*f 1 1 0 0 3 3 2 2 5 5 4 4 7 7 6 6 9 9 8 8 b b a a d d
  //   c c f f e e 0 1 2 3 4 5 6 7 8 9 a b c d e f 10 11 12 13 14 15 16 17 18 19 1a 1b 1c 1d 1e 1f 2 3 2 3
  //   2 3 2 3 2 3 2 3 2 3 2 3 2 3 2 3 2 3 2 3 2 3 2 3 2 3 2 3 0 0 1 1 2 2 3 3 4 4 5 5 6 6 7 7 8 8 9 9 a a
  //   b b c c d d e e f f 2 3 3 4 4 5 5 6 6 7 7 8 8 9 9 a a b b c c d d e e f f 10 10 11 11 12 d e e f f
  //   10 10 11 11 12 12 13 13 14 14 15 15 16 16 17 17 18 18 19 19 1a 1a 1b 1b 1c 1c 1d 4*0 4*2 4*0 4*2 4*0
  //   4*2 4*0 6*2 3 3 2 2 3 3 6 6 7 7 6 6 7 7 a a b b a a b b e e f f e e f f 2 2 3 3 0 0 1 1 6 6 7 7 4 4
  //   5 5 a a b b 8 8 9 9 e e f f c c d d 0 1 2 3 4 5 6 7 8 9 a b c d e f 10 11 12 13 14 15 16 17 18 19 1a
  //   1b 1c 1d 1e 1f 4 5 4 5 4 5 4 5 4 5 4 5 4 5 4 5 4 5 4 5 4 5 4 5 4 5 4 5 4 5 4 5 0 0 1 1 2 2 3 3 4 4 5
  //   5 6 6 7 7 8 8 9 9 a a b b c c d d e e f f 3 4 4 5 5 6 6 7 7 8 8 9 9 a a b b c c d d e e f f 10 10 11
  //   11 12 12 13 c d d e e f f 10 10 11 11 12 12 13 13 14 14 15 15 16 16 17 17 18 18 19 19 1a 1a 1b 1b 1c
  //   0 0 1 1 2 2 3 3 0 0 1 1 2 2 3 3 0 0 1 1 2 2 3 3 0 0 1 1 2 2 10*3 8*7 8*b 8*f 3 3 2 2 1 1 0 0 7 7 6 6
  //   5 5 4 4 b b a a 9 9 8 8 f f e e d d c c 0 1 2 3 4 5 6 7 8 9 a b c d e f 10 11 12 13 14 15 16 17 18
  //   19 1a 1b 1c 1d 1e 1f 6 7 6 7 6 7 6 7 6 7 6 7 6 7 6 7 6 7 6 7 6 7 6 7 6 7 6 7 6 7 6 7 0 0 1 1 2 2 3 3
  //   4 4 5 5 6 6 7 7 8 8 9 9 a a b b c c d d e e f f 4 5 5 6 6 7 7 8 8 9 9 a a b b c c d d e e f f 10 10
  //   11 11 12 12 13 13 14 b c c d d e e f f 10 10 11 11 12 12 13 13 14 14 15 15 16 16 17 17 18 18 19 19
  //   1a 1a 1b 8*0 8*4 8*0 10*4 5 5 6 6 7 7 4 4 5 5 6 6 7 7 c c d d e e f f c c d d e e f f 4 4 5 5 6 6 7
  //   7 0 0 1 1 2 2 3 3 c c d d e e f f 8 8 9 9 a a b b 0 1 2 3 4 5 6 7 8 9 a b c d e f 10 11 12 13 14 15
  //   16 17 18 19 1a 1b 1c 1d 1e 1f 8 9 8 9 8 9 8 9 8 9 8 9 8 9 8 9 8 9 8 9 8 9 8 9 8 9 8 9 8 9 8 9 0 0 1
  //   1 2 2 3 3 4 4 5 5 6 6 7 7 8 8 9 9 a a b b c c d d e e f f 5 6 6 7 7 8 8 9 9 a a b b c c d d e e f f
  //   10 10 11 11 12 12 13 13 14 14 15 a b b c c d d e e f f 10 10 11 11 12 12 13 13 14 14 15 15 16 16 17
  //   17 18 18 19 19 1a 0 0 1 1 0 0 1 1 4 4 5 5 4 4 5 5 0 0 1 1 0 0 1 1 4 4 5 5 4 4 6*5 4*7 4*5 4*7 4*d
  //   4*f 4*d 4*f 5 5 4 4 7 7 6 6 1 1 0 0 3 3 2 2 d d c c f f e e 9 9 8 8 b b a a 0 1 2 3 4 5 6 7 8 9 a b
  //   c d e f 10 11 12 13 14 15 16 17 18 19 1a 1b 1c 1d 1e 1f a b a b a b a b a b a b a b a b a b a b a b
  //   a b a b a b a b a b 0 0 1 1 2 2 3 3 4 4 5 5 6 6 7 7 8 8 9 9 a a b b c c d d e e f f 6 7 7 8 8 9 9 a
  //   a b b c c d d e e f f 10 10 11 11 12 12 13 13 14 14 15 15 16 9 a a b b c c d d e e f f 10 10 11 11
  //   12 12 13 13 14 14 15 15 16 16 17 17 18 18 19 4*0 4*2 4*4 4*6 4*0 4*2 4*4 6*6 7 7 6 6 7 7 6 6 7 7 6 6
  //   7 7 e e f f e e f f e e f f e e f f 6 6 7 7 4 4 5 5 2 2 3 3 0 0 1 1 e e f f c c d d a a b b 8 8 9 9
  //   0 1 2 3 4 5 6 7 8 9 a b c d e f 10 11 12 13 14 15 16 17 18 19 1a 1b 1c 1d 1e 1f c d c d c d c d c d
  //   c d c d c d c d c d c d c d c d c d c d c d 0 0 1 1 2 2 3 3 4 4 5 5 6 6 7 7 8 8 9 9 a a b b c c d d
  //   e e f f 7 8 8 9 9 a a b b c c d d e e f f 10 10 11 11 12 12 13 13 14 14 15 15 16 16 17 8 9 9 a a b b
  //   c c d d e e f f 10 10 11 11 12 12 13 13 14 14 15 15 16 16 17 17 18 0 0 1 1 2 2 3 3 4 4 5 5 6 6 7 7 0
  //   0 1 1 2 2 3 3 4 4 5 5 6 6 18*7 16*f 7 7 6 6 5 5 4 4 3 3 2 2 1 1 0 0 f f e e d d c c b b a a 9 9 8 8
  //   0 1 2 3 4 5 6 7 8 9 a b c d e f 10 11 12 13 14 15 16 17 18 19 1a 1b 1c 1d 1e 1f e f e f e f e f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
  //   contents of rom_7 (hex, n*v repeats v):
  //   0 1 1 2 2 3 3 4 4 5 5 6 6 7 7 8 8 9 9 a a b b c c d d e e f f 10 10 11 11 12 12 13 13 14 14 15 15 16
  //   16 17 17 18 18 19 19 1a 1a 1b 1b 1c 1c 1d 1d 1e 1e 1f 1f 35*0 1 1 2 2 3 3 4 4 5 5 6 6 7 7 8 8 9 9 a
  //   a b b c c d d e e f f 0 0 1 1 2 2 3 3 4 4 5 5 6 6 7 7 8 8 9 9 a a b b c c d d e e f f 0 1 2 3 4 5 6
  //   7 8 9 a b c d e f 10 11 12 13 14 15 16 17 18 19 1a 1b 1c 1d 1e 1f 0 1 0 1 0 1 0 1 0 1 0 1 0 1 0 1 0
  //   1 0 1 0 1 0 1 0 1 0 1 0 1 0 1 0 0 1 1 2 2 3 3 4 4 5 5 6 6 7 7 8 8 9 9 a a b b c c d d e e f f 1 2 2
  //   3 3 4 4 5 5 6 6 7 7 8 8 9 9 a a b b c c d d e e f f 10 10 11 f 10 10 11 11 12 12 13 13 14 14 15 15
  //   16 16 17 17 18 18 19 19 1a 1a 1b 1b 1c 1c 1d 1d 1e 1e 1f 0 0 1 1 0 0 1 1 0 0 1 1 0 0 1 1 0 0 1 1 0 0
  //   1 1 0 0 1 1 0 0 6*1 4*3 4*5 4*7 4*9 4*b 4*d 4*f 1 1 0 0 3 3 2 2 5 5 4 4 7 7 6 6 9 9 8 8 b b a a d d
  //   c c f f e e 0 1 2 3 4 5 6 7 8 9 a b c d e f 10 11 12 13 14 15 16 17 18 19 1a 1b 1c 1d 1e 1f 2 3 2 3
  //   2 3 2 3 2 3 2 3 2 3 2 3 2 3 2 3 2 3 2 3 2 3 2 3 2 3 2 3 0 0 1 1 2 2 3 3 4 4 5 5 6 6 7 7 8 8 9 9 a a
  //   b b c c d d e e f f 2 3 3 4 4 5 5 6 6 7 7 8 8 9 9 a a b b c c d d e e f f 10 10 11 11 12 e f f 10 10
  //   11 11 12 12 13 13 14 14 15 15 16 16 17 17 18 18 19 19 1a 1a 1b 1b 1c 1c 1d 1d 1e 4*0 4*2 4*0 4*2 4*0
  //   4*2 4*0 6*2 3 3 2 2 3 3 6 6 7 7 6 6 7 7 a a b b a a b b e e f f e e f f 2 2 3 3 0 0 1 1 6 6 7 7 4 4
  //   5 5 a a b b 8 8 9 9 e e f f c c d d 0 1 2 3 4 5 6 7 8 9 a b c d e f 10 11 12 13 14 15 16 17 18 19 1a
  //   1b 1c 1d 1e 1f 4 5 4 5 4 5 4 5 4 5 4 5 4 5 4 5 4 5 4 5 4 5 4 5 4 5 4 5 4 5 4 5 0 0 1 1 2 2 3 3 4 4 5
  //   5 6 6 7 7 8 8 9 9 a a b b c c d d e e f f 3 4 4 5 5 6 6 7 7 8 8 9 9 a a b b c c d d e e f f 10 10 11
  //   11 12 12 13 d e e f f 10 10 11 11 12 12 13 13 14 14 15 15 16 16 17 17 18 18 19 19 1a 1a 1b 1b 1c 1c
  //   1d 0 0 1 1 2 2 3 3 0 0 1 1 2 2 3 3 0 0 1 1 2 2 3 3 0 0 1 1 2 2 10*3 8*7 8*b 8*f 3 3 2 2 1 1 0 0 7 7
  //   6 6 5 5 4 4 b b a a 9 9 8 8 f f e e d d c c 0 1 2 3 4 5 6 7 8 9 a b c d e f 10 11 12 13 14 15 16 17
  //   18 19 1a 1b 1c 1d 1e 1f 6 7 6 7 6 7 6 7 6 7 6 7 6 7 6 7 6 7 6 7 6 7 6 7 6 7 6 7 6 7 6 7 0 0 1 1 2 2
  //   3 3 4 4 5 5 6 6 7 7 8 8 9 9 a a b b c c d d e e f f 4 5 5 6 6 7 7 8 8 9 9 a a b b c c d d e e f f 10
  //   10 11 11 12 12 13 13 14 c d d e e f f 10 10 11 11 12 12 13 13 14 14 15 15 16 16 17 17 18 18 19 19 1a
  //   1a 1b 1b 1c 8*0 8*4 8*0 10*4 5 5 6 6 7 7 4 4 5 5 6 6 7 7 c c d d e e f f c c d d e e f f 4 4 5 5 6 6
  //   7 7 0 0 1 1 2 2 3 3 c c d d e e f f 8 8 9 9 a a b b 0 1 2 3 4 5 6 7 8 9 a b c d e f 10 11 12 13 14
  //   15 16 17 18 19 1a 1b 1c 1d 1e 1f 8 9 8 9 8 9 8 9 8 9 8 9 8 9 8 9 8 9 8 9 8 9 8 9 8 9 8 9 8 9 8 9 0 0
  //   1 1 2 2 3 3 4 4 5 5 6 6 7 7 8 8 9 9 a a b b c c d d e e f f 5 6 6 7 7 8 8 9 9 a a b b c c d d e e f
  //   f 10 10 11 11 12 12 13 13 14 14 15 b c c d d e e f f 10 10 11 11 12 12 13 13 14 14 15 15 16 16 17 17
  //   18 18 19 19 1a 1a 1b 0 0 1 1 0 0 1 1 4 4 5 5 4 4 5 5 0 0 1 1 0 0 1 1 4 4 5 5 4 4 6*5 4*7 4*5 4*7 4*d
  //   4*f 4*d 4*f 5 5 4 4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
endmodule
